# Fritzing sketch GLCD-LG128643-SMLYH6V-V001 (saved by Fritzing 0.9.4)
breadboards: 1

parts:
  GLCD_128x1 = 128 x 64 Graphic LCD
  부품1 = Arduino Uno (Rev3)
  R1 = TRIMPOT [package=3386u]
  S1 = Toggle Switch [package=THT]
  S2 = Toggle Switch [package=THT]
  mono_104 = Ceramic Capacitor [capacitance=100nF package="100 mil [THT, multilayer]"]
  Register_200ohm~ = Resistor [tolerance=±5% resistance=220 package=THT]
  mono104 = Ceramic Capacitor [capacitance=100nF package="100 mil [THT, multilayer]"]
  Register_200ohm_~ = Resistor [tolerance=±5% resistance=220 package=THT]

nets:
  N1: GLCD_128x1.1_Vss, GLCD_128x1.20_K(-), 부품1.GND, R1.CCW, Register_200ohm~.Pin_0, Register_200ohm_~.Pin_0
  N2: GLCD_128x1.2_Vdd, GLCD_128x1.19_A(+), 부품1.5V, S1.L1, S2.L1
  N3: GLCD_128x1.3_Vo, R1.WIPER
  N4: GLCD_128x1.4_D/I, 부품1.A3
  N5: GLCD_128x1.5_R/W, 부품1.A2
  N6: GLCD_128x1.6_Enable, 부품1.A4/SDA
  N7: GLCD_128x1.7_DB0, 부품1.D8
  N8: GLCD_128x1.8_DB1, 부품1.D9_PWM
  N9: GLCD_128x1.9_BD2, 부품1.D10_PWM/SS
  N10: GLCD_128x1.10_DB3, 부품1.D11_PWM/MOSI
  N11: GLCD_128x1.11_DB4, 부품1.D4
  N12: GLCD_128x1.12_DB5, 부품1.D5_PWM
  N13: GLCD_128x1.13_DB6, 부품1.D6_PWM
  N14: GLCD_128x1.14_DB7, 부품1.D7
  N15: GLCD_128x1.15_CS1, 부품1.A0
  N16: GLCD_128x1.16_CS2, 부품1.A1
  N17: GLCD_128x1.17_RST, 부품1.RESET
  N18: GLCD_128x1.18_Vout, R1.CW
  N19: 부품1.D2, mono104.0
  N20: 부품1.D3_PWM, mono_104.0
  N21: S1.COM, mono104.1, Register_200ohm_~.Pin_1
  N22: S2.COM, mono_104.1, Register_200ohm~.Pin_1

notes:
  limit sensor (1)
  limit sensor (2)
  mono 104
  GLCD
  200 ~ 1k ohm
  10K OR 20K
