# Fritzing sketch GLCD-LG128643-SMLYH6V (saved by Fritzing 0.9.4)
breadboards: 1

parts:
  GLCD_128x1 = 128 x 64 Graphic LCD
  부품1 = Arduino Uno (Rev3)
  R1 = TRIMPOT [package=3386u]

nets:
  N1: GLCD_128x1.1_Vss, GLCD_128x1.20_K(-), 부품1.GND, R1.CCW
  N2: GLCD_128x1.2_Vdd, GLCD_128x1.19_A(+), 부품1.5V
  N3: GLCD_128x1.3_Vo, R1.WIPER
  N4: GLCD_128x1.4_D/I, 부품1.A3
  N5: GLCD_128x1.5_R/W, 부품1.A2
  N6: GLCD_128x1.6_Enable, 부품1.A4/SDA
  N7: GLCD_128x1.7_DB0, 부품1.D8
  N8: GLCD_128x1.8_DB1, 부품1.D9_PWM
  N9: GLCD_128x1.9_BD2, 부품1.D10_PWM/SS
  N10: GLCD_128x1.10_DB3, 부품1.D11_PWM/MOSI
  N11: GLCD_128x1.11_DB4, 부품1.D4
  N12: GLCD_128x1.12_DB5, 부품1.D5_PWM
  N13: GLCD_128x1.13_DB6, 부품1.D6_PWM
  N14: GLCD_128x1.14_DB7, 부품1.D7
  N15: GLCD_128x1.15_CS1, 부품1.A0
  N16: GLCD_128x1.16_CS2, 부품1.A1
  N17: GLCD_128x1.17_RST, 부품1.RESET
  N18: GLCD_128x1.18_Vout, R1.CW
