# Fritzing sketch about esp8266-01 (saved by Fritzing 0.9.4)
breadboards: 1

parts:
  R1 = Resistor [tolerance=±1% resistance=1k package=THT]
  R2 = Resistor [tolerance=±1% resistance=1k package=THT]
  R3 = Resistor [tolerance=±1% resistance=1k package=THT]
  아두이노_우노_R3 = Arduino Uno (Rev3)
  part = ESP8266 WiFi Module [part_number=ESP8266]

nets:
  N1: R1.Pin_0, R2.Pin_1
  N2: R1.Pin_1, 아두이노_우노_R3.GND
  N3: R2.Pin_0, R3.Pin_1, part.RX
  N4: R3.Pin_0, 아두이노_우노_R3.D1/TX
  N5: 아두이노_우노_R3.D0/RX, part.TX
